// Logisim project Stefan Grulovic - CS310 Project.circ as structural Verilog: 1 circuit, main circuit main
module main (
  input  in_1,
  input  in_2,
  input  in_3,
  input  in_4,
  input  E,
  output out_6,
  output out_7,
  output out_8,
  output out_9,
  output U,
  output V,
  output W,
  output X
);

  wire and_1_out, and_2_out, and_3_out, and_4_out, and_5_out, and_6_out, and_7_out, and_8_out, and_9_out,
       and_10_out, and_12_out, and_13_out, and_14_out, and_15_out, and_16_out, and_17_out, and_18_out,
       and_19_out, not_2_out, not_3_out, not_4_out, not_5_out, not_6_out, or_1_out, or_2_out, or_3_out,
       or_4_out, or_5_out, or_6_out, or_7_out, or_12_out;

  not not_1 (V, in_4);
  not not_2 (not_2_out, in_2);
  not not_3 (not_3_out, in_3);
  not not_4 (not_4_out, E);
  or or_1 (or_1_out, in_4, in_3);
  or or_2 (or_2_out, in_2, in_1);
  and and_1 (and_1_out, not_3_out, V);
  and and_2 (and_2_out, in_3, in_4);
  and and_3 (and_3_out, not_2_out, in_3);
  and and_4 (and_4_out, in_2, not_3_out);
  or or_3 (or_3_out, in_3, E);
  or or_4 (or_4_out, in_2, in_3);
  and and_5 (and_5_out, in_2, E, or_1_out);
  and and_6 (and_6_out, or_2_out, not_4_out);
  and and_7 (and_7_out, not_2_out, E, or_1_out);
  and and_8 (and_8_out, in_2, not_3_out, V);
  or or_5 (or_5_out, and_1_out, and_2_out);
  or or_6 (or_6_out, and_3_out, and_4_out);
  and and_9 (and_9_out, V, or_3_out);
  and and_10 (and_10_out, not_3_out, in_4, not_4_out);
  and and_11 (U, in_1, or_4_out);
  and and_12 (and_12_out, not_2_out, in_4);
  and and_13 (and_13_out, in_2, V);
  and and_14 (and_14_out, E, or_5_out);
  and and_15 (and_15_out, or_6_out, not_4_out);
  or or_7 (or_7_out, and_12_out, and_13_out);
  not not_5 (not_5_out, in_1);
  or or_8 (out_6, in_1, and_5_out);
  or or_9 (out_7, and_6_out, and_7_out, and_8_out);
  or or_10 (out_8, and_14_out, and_15_out);
  or or_11 (out_9, and_9_out, and_10_out);
  not not_6 (not_6_out, in_1);
  or or_12 (or_12_out, not_2_out, and_16_out);
  and and_16 (and_16_out, not_3_out, V);
  and and_17 (and_17_out, in_1, in_4);
  and and_18 (and_18_out, in_3, or_7_out);
  and and_19 (and_19_out, not_5_out, not_2_out, not_3_out, V);
  and and_20 (W, not_6_out, or_12_out);
  or or_13 (X, and_17_out, and_18_out, and_19_out);
  LED led_1 (.in(U));

  // Notes on the sheet:
  //   CS310 - Project
  //   Stefan Grulovic (20150280)
  //   A,B,C,D - 4 BIT INPUT
  //   A      B     C     D       E
  //   0- Gray Code
  //   1- XS3 Code
  //   Q,R,S,T - 4 BIT OUTPUT
  //   Q      R      S     T        U
  //   1- ERROR
  //   0- NO ERROR
  //   EXTRA:
  //   0- ODD
  //   1- EVEN
  //   0- Bigger than 5
  //   1- Smaller than 5
  //   0- Not Divisible by 3
  //   1- Divisible by 3
endmodule
